// Logisim project Assignment_2.circ as structural Verilog
module main (
  input  in_1,
  input  in_2,
  input  in_3,
  input  in_4,
  input  in_5,
  input  in_6,
  input  in_7,
  input  in_8,
  input  in_9,
  input  in_10,
  input  in_11,
  input  in_12,
  input  in_13,
  input  [2:0] in_14,
  input  in_15,
  input  [2:0] in_16,
  output out_17,
  output out_18,
  output out_19
);

  wire vote25_1_result;
  wire [7:0] display_letters_1_display, problem5_1_display;
  wire [14:0] dipswitch_2_sw15;
  wire [24:0] dipswitch_1_sw25;

  And_Or and_or_1 (.a(in_1), .b(in_2), .c(in_3), .d(in_4), .out1(out_17), .out2(out_18));
  mux8_1 mux8_1_1 (
    .a(in_5), .b(in_6), .c(in_8), .d(in_9), .e(in_10), .f(in_11), .g(in_12), .i(in_13), .ch(in_14),
    .data(out_19));
  display_letters display_letters_1 (.en(in_15), .data(in_16), .display(display_letters_1_display));
  DipSwitch #(.number(25)) dipswitch_1 (
    .sw1(dipswitch_1_sw25[24]), .sw2(dipswitch_1_sw25[23]), .sw3(dipswitch_1_sw25[22]),
    .sw4(dipswitch_1_sw25[21]), .sw5(dipswitch_1_sw25[20]), .sw6(dipswitch_1_sw25[19]),
    .sw7(dipswitch_1_sw25[18]), .sw8(dipswitch_1_sw25[17]), .sw9(dipswitch_1_sw25[16]),
    .sw10(dipswitch_1_sw25[15]), .sw11(dipswitch_1_sw25[14]), .sw12(dipswitch_1_sw25[13]),
    .sw13(dipswitch_1_sw25[12]), .sw14(dipswitch_1_sw25[11]), .sw15(dipswitch_1_sw25[10]),
    .sw16(dipswitch_1_sw25[9]), .sw17(dipswitch_1_sw25[8]), .sw18(dipswitch_1_sw25[7]),
    .sw19(dipswitch_1_sw25[6]), .sw20(dipswitch_1_sw25[5]), .sw21(dipswitch_1_sw25[4]),
    .sw22(dipswitch_1_sw25[3]), .sw23(dipswitch_1_sw25[2]), .sw24(dipswitch_1_sw25[1]),
    .sw25(dipswitch_1_sw25[0]));
  DipSwitch #(.number(15)) dipswitch_2 (
    .sw1(dipswitch_2_sw15[14]), .sw2(dipswitch_2_sw15[13]), .sw3(dipswitch_2_sw15[12]),
    .sw4(dipswitch_2_sw15[11]), .sw5(dipswitch_2_sw15[10]), .sw6(dipswitch_2_sw15[9]),
    .sw7(dipswitch_2_sw15[8]), .sw8(dipswitch_2_sw15[7]), .sw9(dipswitch_2_sw15[6]),
    .sw10(dipswitch_2_sw15[5]), .sw11(dipswitch_2_sw15[4]), .sw12(dipswitch_2_sw15[3]),
    .sw13(dipswitch_2_sw15[2]), .sw14(dipswitch_2_sw15[1]), .sw15(dipswitch_2_sw15[0]));
  _7_Segment_Display u_7_segment_display_1 (
    .g(display_letters_1_display[1]), .f(display_letters_1_display[2]), .a(display_letters_1_display[7]),
    .b(display_letters_1_display[6]), .e(display_letters_1_display[3]), .d(display_letters_1_display[4]),
    .c(display_letters_1_display[5]), .dp(display_letters_1_display[0]));
  LED led_1 (.in(vote25_1_result));
  vote25 vote25_1 (.vt(dipswitch_1_sw25), .result(vote25_1_result));
  problem5 problem5_1 (.en(in_7), .vt(dipswitch_2_sw15), .display(problem5_1_display));
  _7_Segment_Display u_7_segment_display_2 (
    .g(problem5_1_display[1]), .f(problem5_1_display[2]), .a(problem5_1_display[7]),
    .b(problem5_1_display[6]), .e(problem5_1_display[3]), .d(problem5_1_display[4]),
    .c(problem5_1_display[5]), .dp(problem5_1_display[0]));
endmodule

// VHDL entity And_Or, as the project stores it:
--library and package
LIBRARY ieee;
USE ieee.std_logic_1164.all;
USE ieee.std_logic_arith.all;
USE ieee.std_logic_unsigned.all;


--entity (input&output)
ENTITY And_Or IS
	PORT (
		a,b,c,d		:IN  std_logic;                    
		out1,out2		:OUT std_logic
	);
END And_Or;

--architecture
ARCHITECTURE bhv OF And_Or IS
BEGIN
	
	out1 <= a and b and c and d;
	out2 <= a or b or c or d;
END ARCHITECTURE bhv;

// VHDL entity mux8_1, as the project stores it:
--library and package
LIBRARY ieee;
USE ieee.std_logic_1164.all;
USE ieee.std_logic_arith.all;
USE ieee.std_logic_unsigned.all;


--entity (input&output)
ENTITY mux8_1 IS
	PORT (
		a,b,c,d,e,f,g,i	:IN  std_logic;       
		ch				:IN	std_logic_vector(2 downto 0);
		data				:OUT std_logic
	);
END mux8_1;

--architecture
ARCHITECTURE bhv OF mux8_1 IS
BEGIN
	process(a,b,c,d,e,f,g,i,ch)
	begin
		case ch is
			when "000" => data <= a;
			when "001" => data <= b;
			when "010" => data <= c;
			when "011" => data <= d;
			when "100" => data <= e;
			when "101" => data <= f;
			when "110" => data <= g;
			when "111" => data <= i;
			when others => data <= '0';
		end case;
	end process;
END ARCHITECTURE bhv;

// VHDL entity display_letters, as the project stores it:
--library and package
LIBRARY ieee;
USE ieee.std_logic_1164.all;
USE ieee.std_logic_arith.all;
USE ieee.std_logic_unsigned.all;

--entity (input&output)
ENTITY display_letters IS
	PORT (
		en			:IN  std_logic;       
		data			:IN	std_logic_vector(2 downto 0);
		display		:OUT std_logic_vector(7 downto 0)
	);
END display_letters;

--architecture
ARCHITECTURE bhv OF display_letters IS
BEGIN
	process(en,data)
	begin
		if en='0' then
			display <= "ZZZZZZZZ";
		else
			case data is
				when "000" => display <= "11101111";
				when "001" => display <= "00111111";
				when "010" => display <= "00011011";
				when "011" => display <= "01111011";
				when "100" => display <= "10001111";
				when "101" => display <= "11110111";
				when others => display <= "00000000";
			end case;
		end if;
	end process;
END ARCHITECTURE bhv;

// VHDL entity vote25, as the project stores it:
--library and package
LIBRARY ieee;
USE ieee.std_logic_1164.all;
USE ieee.std_logic_arith.all;
USE ieee.std_logic_unsigned.all;

--entity (input&output)
ENTITY vote25 IS
	PORT (
		vt			:IN	std_logic_vector(25 downto 1);
		result		:OUT std_logic
	);
END vote25;

--architecture
ARCHITECTURE bhv OF vote25 IS
BEGIN
	process(vt)
	variable sum:integer range 0 to 25;
	begin
		sum:=0;
		for i in 1 to 25 loop
			if (vt(i)='1') then
				sum:=sum+1;
			end if;
		end loop;
		if sum >= 13 then
			result <= '1';
		else
			result <= '0';
		end if;
	end process;
END ARCHITECTURE bhv;

// VHDL entity problem5, as the project stores it:
--library and package
LIBRARY ieee;
USE ieee.std_logic_1164.all;
USE ieee.std_logic_arith.all;
USE ieee.std_logic_unsigned.all;

--entity (input&output)
ENTITY problem5 IS
	PORT (
		en			:IN  std_logic;       
		vt			:IN	std_logic_vector(14 downto 0);
		display		:OUT std_logic_vector(7 downto 0)
	);
END problem5;

--architecture
ARCHITECTURE bhv OF problem5 IS
BEGIN
	process(en,vt)
	variable sum:integer range 0 to 15;
	begin
		if en='0' then
			display <= "ZZZZZZZZ";
		else
			sum:=0;
			for i in 0 to 14 loop
				if (vt(i)='1') then
					sum:=sum+1;
				end if;
			end loop;
			case sum is
				when 0 => display <= "11111100";
				when 1 => display <= "01100000";
				when 2 => display <= "11011010";
				when 3 => display <= "11110010";
				when 4 => display <= "01100110";
				when 5 => display <= "10110110";
				when 6 => display <= "10111110";
				when 7 => display <= "11100100";
				when 8 => display <= "11111110";
				when 9 => display <= "11110110";
				when 10 => display <= "11101111";
				when 11 => display <= "00111111";
				when 12 => display <= "00011011";
				when 13 => display <= "01111011";
				when 14 => display <= "10011111";
				when 15 => display <= "10001111";
				when others => display <= "00000000";
			end case;
		end if;
	end process;
END ARCHITECTURE bhv;
